# Fritzing sketch Projet de conception2 (saved by Fritzing 0.9.4)
breadboards: 1

parts:
  R2 = Photocell (LDR) [package=THT]
  Composant1 = Arduino Uno (Rev3)
  M1 = DC Motor
  Q1 = NPN-Transistor [package="SOT-23 [SMD]"]
  VCC2 = Battery block 9V
  VCC3 = Battery block 9V
  R3 = 1 kΩ Resistor [package=THT]

nets:
  N1: R2.pin_0, Composant1.A0
  N2: R2.pin_1, Composant1.A1, R3.Pin_0
  N3: Composant1.A2, R3.Pin_1
  N4: Composant1.5V, Q1.0
  N5: Composant1.GND, M1.pin_1, Q1.2, VCC3.-
  N6: Composant1.VIN, VCC3.+
  N7: M1.pin_2, VCC2.-
  N8: Q1.1, VCC2.+

custom parts:
  Photocell (LDR): A generic light dependent resistor (LDR)
  1 kΩ Resistor: A generic resistor (0.25W)
